# Fritzing sketch Arduino RCcar (saved by Fritzing 0.9.4)
breadboards: 1

parts:
  부품1 = Arduino Uno (Rev3)
  부품2 = Bluetooth HC-05 Macho  # not connected
  HC-SR04_Sensor_1 = HC-SR04 Ultrasonic Distance Sensor
  J1 = Basic Servo
  M1 = DC Motor  # not connected
  M2 = DC Motor  # not connected
  M3 = DC Motor  # not connected
  M4 = DC Motor  # not connected
  J4 = female pin header, 1 pin [form="♀ (female)"]
  J5 = female pin header, 1 pin [form="♀ (female)"]
  J6 = female pin header, 6 pins [form="♀ (female)"]
  J7 = female pin header, 3 pins [form="♀ (female)"]
  J8 = female pin header, 3 pins [form="♀ (female)"]
  J9 = female pin header, 3 pins [form="♀ (female)"]

nets:
  N1: 부품1.A3, J9.pin3
  N2: 부품1.A4/SDA, J8.pin3
  N3: 부품1.A5/SCL, J7.pin3
  N4: 부품1.D9_PWM, J6.pin3
  N5: 부품1.D10_PWM/SS, J6.pin4
  N6: 부품1.D11_PWM/MOSI, J6.pin5
  N7: 부품1.D12/MISO, HC-SR04_Sensor_1.ECHO
  N8: 부품1.D13/SCK, HC-SR04_Sensor_1.TRIG
  N9: 부품1.D2, J1.pulse
  N10: 부품1.D3_PWM, J6.pin2
  N11: 부품1.D5_PWM, J6.pin1
  N12: 부품1.D6_PWM, J6.pin6
  VCC: 부품1.5V, HC-SR04_Sensor_1.VCC, J1.vcc, J5.pin1
  GND: 부품1.GND, HC-SR04_Sensor_1.GND, J1.gnd, J4.pin1
